# Fritzing sketch connect_battery (saved by Fritzing 0.8.3b)
breadboards: 1

parts:
  Part1 = Arduino Nano (Rev3.0)
  C1 = Capacitor Polarized [package=cpol-radial-1000uf-25v]
  D1 = Rectifier Diode [part_number=1N4001 package="Melf DO-213 AB [SMD]"]
  X2 = X113647 Stepper Driver Board [part_number=X113647 package=board]
  X3 = X113647 Stepper Driver Board [part_number=X113647 package=board]
  MOTOR3 = 28BYJ-48 Stepper Motor
  MOTOR2 = 28BYJ-48 Stepper Motor
  BATT2 = 3xAAA Switchable Battery Pack w/Bare Wire

nets:
  GND: Part1.D1/TX, Part1.GND, X2.GND, X3.GND, BATT2.NEG
  N1: Part1.RESET, C1.-
  N2: Part1.D2, X3.IN1
  N3: Part1.D4, X3.IN2, X3.IN3
  N4: Part1.D5, X3.IN4
  N5: Part1.D6, X2.IN1
  N6: Part1.D7, X2.IN2
  N7: Part1.D8, X2.IN3
  N8: Part1.D9, X2.IN4
  N9: Part1.A7, C1.+, D1.cathode
  N10: D1.anode, X2.+V, X3.+V, BATT2.POS
  N11: X2.BLUE, MOTOR2.BLUE
  N12: X2.PINK, MOTOR2.PINK
  N13: X2.YELLOW, MOTOR2.YELLOW
  N14: X2.ORANGE, MOTOR2.ORANGE
  N15: X2.RED, MOTOR2.RED
  N16: X3.BLUE, MOTOR3.BLUE
  N17: X3.PINK, MOTOR3.PINK
  N18: X3.YELLOW, MOTOR3.YELLOW
  N19: X3.ORANGE, MOTOR3.ORANGE
  N20: X3.RED, MOTOR3.RED

custom parts:
  X113647 Stepper Driver Board: A common stepper motor driver board based on ULN2003APG darlington array
  28BYJ-48 Stepper Motor: 28BYJ-48 gear-reduction stepper motor (small)
  3xAAA Switchable Battery Pack w/Bare Wire: 3xAAA Switchable Battery Pack w/Bare Wire Connectors
