# Fritzing sketch connect_power_to_motors (saved by Fritzing 0.8.3b)
breadboards: 1

parts:
  Part1 = Arduino Nano (Rev3.0)
  C1 = Capacitor Polarized [package=cpol-radial-1000uf-25v]
  D1 = Rectifier Diode [part_number=1N4001 package="Melf DO-213 AB [SMD]"]
  X2 = X113647 Stepper Driver Board [part_number=X113647 package=board]
  X3 = X113647 Stepper Driver Board [part_number=X113647 package=board]

nets:
  GND: Part1.D1/TX, Part1.GND, X2.GND, X3.GND
  N1: Part1.RESET, C1.-
  N2: Part1.A7, C1.+, D1.cathode
  N3: D1.anode, X2.+V, X3.+V

custom parts:
  X113647 Stepper Driver Board: A common stepper motor driver board based on ULN2003APG darlington array
