# Fritzing sketch ShonkESP-flashing (saved by Fritzing 0.9.0b)
breadboards: 1

parts:
  J1 = rounded female pin header, 6 pins [form="♀ (female rounded)"]
  Part1 = Open-Smart ESP-01 Adapter
  U2 = ESP8266 WiFi Module [part_number=ESP8266]

nets:
  N1: J1.pin1, Part1.GND, U2.GPIO_0
  N2: J1.pin3, Part1.VCC
  N3: J1.pin4, Part1.RX
  N4: J1.pin5, Part1.TX

notes:
  Either a 3V3 or 5V variant of FTDI-style USB/serial cable. I connect this directly to the breadboard with extra-tall double-male header pins, but Shonky male-male wires are probably closer to hand.
  Booting with GPIO_0 low triggers flashing mode. Carefully but firmly touch the flying ground wire to GPIO_0 on the ESP-01 directly, holding it there while plugging the USB end of your FTDI cable in (or otherwise powering up the ESP-01). I can only just barely do this without a second pair of hands. Once it has power, you can carefully remove the flying ground wire if you wish. There's no indication of flashing mode besides trying the flashing tool and seeing whether it worked.
  Since you need to get two grounds from one, you can't quite do this with just male-female jumper wires, hence the breadboard. Also you need access to a pin on the ESP-01 that the Adatper doesn't expose, hence showing both.
  Adatper

custom parts:
  ESP8266 WiFi Module: Generic WiFi Module based on the ESP8266 with onboard PCB antenna and UART communications
