# Fritzing sketch connect_power_supply (saved by Fritzing 0.8.3b)
breadboards: 1

parts:
  Part1 = Arduino Nano (Rev3.0)
  C1 = Capacitor Polarized [package=cpol-radial-1000uf-25v]
  D1 = Rectifier Diode [part_number=1N4001 package="Melf DO-213 AB [SMD]"]

nets:
  N1: Part1.D1/TX, Part1.GND, C1.-
  N2: Part1.5V, C1.+, D1.cathode
