# Fritzing sketch connect_power_supply_esp (saved by Fritzing 0.9.0b)
breadboards: 1

parts:
  C1 = Capacitor Polarized [package=cpol-radial-1000uf-25v]
  D1 = Rectifier Diode [part_number=1N4001 package="Melf DO-213 AB [SMD]"]
  Part1 = Arduino Nano (Rev3.0)
  Part2 = Open-Smart ESP-01 Adapter

nets:
  N1: C1.+, D1.cathode, Part1.5V
  GND: C1.-, Part1.GND, Part2.GND
  N2: D1.anode, Part1.RESET, Part2.VCC
  N3: Part1.D1/TX, Part2.RX
  N4: Part1.D0/RX, Part2.TX
