# Fritzing sketch just_led (saved by Fritzing 0.8.3b)
breadboards: 1

parts:
  Part1 = Arduino Nano (Rev3.0)
  LED1 = LED - 5mm [color="Infrared (940nm)" package="5 mm [THT]"]
  D1 = Diode [package=diode-1n4148]
  C1 = Capacitor Polarized [package=cpol-radial-1000uf-25v]

nets:
  N1: Part1.D1/TX, Part1.GND, LED1.cathode, C1.-
  N2: Part1.5V, D1.A, C1.+
  N3: Part1.D13/SCK, LED1.anode
