# Fritzing sketch shonkbot_swarm (saved by Fritzing 0.8.3b)
breadboards: 1

parts:
  J1 = Piezo Speaker
  Part1 = Arduino Nano (Rev3.0)
  LED1 = LED - 5mm [color="Infrared (940nm)" package="5 mm [THT]"]
  Q1 = LTR-301 [package=ltr-301]
  D1 = Diode [package=diode-1n4148]
  R4 = Resistor [tolerance=±5% resistance=10k package=THT]
  MOTOR2 = 28BYJ-48 Stepper Motor
  X2 = X113647 Stepper Driver Board [part_number=X113647 package=board]
  MOTOR3 = 28BYJ-48 Stepper Motor
  X3 = X113647 Stepper Driver Board [part_number=X113647 package=board]
  BATT1 = 3xAAA Switchable Battery Pack w/Bare Wire
  C1 = Capacitor Polarized [package=cpol-radial-1000uf-25v]
  LED2 = LED - 5mm [color="Infrared (940nm)" package="5 mm [THT]"]

nets:
  GND: J1.pin1, Part1.D1/TX, Part1.GND, Part1.D12/MISO, Part1.A0, LED1.cathode, Q1.C, Q1.E, X2.GND, X3.GND, BATT1.NEG, C1.-, LED2.cathode, LED2.anode
  N1: J1.pin2, Part1.D10
  N2: Part1.D2, X3.IN1
  N3: Part1.D3, X3.IN2
  N4: Part1.D4, X3.IN3
  N5: Part1.D5, X3.IN4
  N6: Part1.D6, X2.IN1
  N7: Part1.D7, X2.IN2
  N8: Part1.D8, X2.IN3
  N9: Part1.D9, X2.IN4
  N10: Part1.5V, D1.A, R4.Pin_0, C1.+
  N11: Part1.D13/SCK, LED1.anode
  N12: MOTOR2.BLUE, X2.BLUE
  N13: MOTOR2.PINK, X2.PINK
  N14: MOTOR2.RED, X2.RED
  N15: MOTOR2.ORANGE, X2.ORANGE
  N16: MOTOR2.YELLOW, X2.YELLOW
  N17: X2.+V, X3.+V, BATT1.POS
  N18: MOTOR3.BLUE, X3.BLUE
  N19: MOTOR3.PINK, X3.PINK
  N20: MOTOR3.RED, X3.RED
  N21: MOTOR3.ORANGE, X3.ORANGE
  N22: MOTOR3.YELLOW, X3.YELLOW

custom parts:
  28BYJ-48 Stepper Motor: 28BYJ-48 gear-reduction stepper motor (small)
  X113647 Stepper Driver Board: A common stepper motor driver board based on ULN2003APG darlington array
  3xAAA Switchable Battery Pack w/Bare Wire: 3xAAA Switchable Battery Pack w/Bare Wire Connectors
