# Fritzing sketch ir (saved by Fritzing 0.8.3b)
breadboards: 1

parts:
  Part1 = Arduino Nano (Rev3.0)
  LED1 = LED - 5mm [color="Infrared (940nm)" package="5 mm [THT]"]
  D1 = Diode [package=diode-1n4148]
  C1 = Capacitor Polarized [package=cpol-radial-1000uf-25v]
  R4 = Resistor [tolerance=±5% resistance=10k package=THT]
  Q1 = LTR-301 [package=ltr-301]

nets:
  N1: Part1.D1/TX, Part1.GND, LED1.cathode, C1.-, Q1.E
  N2: Part1.5V, D1.A, C1.+, R4.Pin_0
  N3: Part1.A0, R4.Pin_1, Q1.C
  N4: Part1.D13/SCK, LED1.anode
