# Fritzing sketch quickshonk (saved by Fritzing 0.9.0b)
breadboards: 4

parts:
  Part1 = Arduino Nano (Rev3.0)
  VCC1 = Battery
  C1 = Electrolytic Capacitor [capacitance=1µF package="100 mil [THT, electrolytic]"]
  M1 = DC Motor
  M2 = DC Motor
  J1 = Piezo Speaker
  D1 = Rectifier Diode [part_number=1N4001 package="300 mil [THT]"]
  Part2 = Arduino Nano (Rev3.0)
  IC2 = H-Bridge [package=THT]
  Part3 = Arduino Nano (Rev3.0)
  IC3 = H-Bridge [package=THT]
  Part4 = Arduino Nano (Rev3.0)  # not connected
  IC4 = H-Bridge [package=THT]  # not connected
  H-bridge = H-Bridge [package=THT]

nets:
  GND: Part1.GND, VCC1.-, C1.-, J1.pin1, H-bridge.GND1, H-bridge.GND2, H-bridge.GND3, H-bridge.GND4
  N1: Part1.D10, J1.pin2
  N2: Part1.5V, D1.cathode
  N3: VCC1.+, C1.+, D1.anode, H-bridge.VCC2, H-bridge.VCC1
  N4: M1.pin_1, H-bridge.4Y
  N5: M1.pin_2, H-bridge.3Y
  N6: M2.pin_1, H-bridge.2Y
  N7: M2.pin_2, H-bridge.1Y
  N8: Part2.D7, IC2.1A
  N9: Part2.D8, IC2.2A
  N10: Part2.D9, IC2.1_2EN
  N11: Part3.D4, IC3.3A
  N12: Part3.D5, IC3.4A
  N13: Part3.D6, IC3.3_4EN

notes:
  This diagram covers control wiring for the motor on the right side.
  This diagram covers control wiring for the motor on the left side.
  This diagram covers control wiring for the ultrasonic sensor.
  This diagram covers the overall framework, and power.
  Back of the bot. If you want to keep the pen hole free, the battery box will need to hang off the back a bit.
  Bot's right side.
  Bot's left side.
  The Nano's D12 pin should be in breadboard hole h1 on most breadboards. The breadboards in these diagrams are two holes longer than real boards!
  This must be a 3xAA box, only I can't find an icon for that.
