# Fritzing sketch shonkbot (saved by Fritzing 0.8.3b)
breadboards: 1

parts:
  J1 = Piezo Speaker
  Part1 = Arduino Nano (Rev3.0)
  C1 = Capacitor Polarized [package=cpol-radial-1000uf-25v]
  LED1 = LED - 5mm [color="Infrared (940nm)" package="5 mm [THT]"]
  Q1 = LTR-301 [package=ltr-301]
  D1 = Diode [package=diode-1n4148]
  R4 = Resistor [tolerance=±5% resistance=10k package=THT]
  MOTOR2 = 28BYJ-48 Stepper Motor
  X2 = X113647 Stepper Driver Board [part_number=X113647 package=board]
  MOTOR3 = 28BYJ-48 Stepper Motor
  X3 = X113647 Stepper Driver Board [part_number=X113647 package=board]
  BATT1 = 3xAAA Switchable Battery Pack w/Bare Wire

nets:
  GND: J1.pin1, Part1.GND, LED1.cathode, Q1.C, Q1.E, R4.Pin_1, X2.GND, X3.GND, BATT1.NEG
  N1: J1.pin2, X2.+V, X3.+V, BATT1.POS
  N2: C1.+, D1.A, R4.Pin_0
  N3: MOTOR2.BLUE, X2.BLUE
  N4: MOTOR2.PINK, X2.PINK
  N5: MOTOR2.RED, X2.RED
  N6: MOTOR2.ORANGE, X2.ORANGE
  N7: MOTOR2.YELLOW, X2.YELLOW
  N8: MOTOR3.BLUE, X3.BLUE
  N9: MOTOR3.PINK, X3.PINK
  N10: MOTOR3.RED, X3.RED
  N11: MOTOR3.ORANGE, X3.ORANGE
  N12: MOTOR3.YELLOW, X3.YELLOW

custom parts:
  28BYJ-48 Stepper Motor: 28BYJ-48 gear-reduction stepper motor (small)
  X113647 Stepper Driver Board: A common stepper motor driver board based on ULN2003APG darlington array
  3xAAA Switchable Battery Pack w/Bare Wire: 3xAAA Switchable Battery Pack w/Bare Wire Connectors
