# Fritzing sketch shonkbot_drawing (saved by Fritzing 0.8.3b)
breadboards: 1

parts:
  J1 = Piezo Speaker
  Part1 = Arduino Nano (Rev3.0)
  D1 = Diode [package=diode-1n4148]
  MOTOR2 = 28BYJ-48 Stepper Motor
  X2 = X113647 Stepper Driver Board [part_number=X113647 package=board]
  MOTOR3 = 28BYJ-48 Stepper Motor
  X3 = X113647 Stepper Driver Board [part_number=X113647 package=board]
  BATT1 = 3xAAA Switchable Battery Pack w/Bare Wire
  C1 = Capacitor Polarized [package=cpol-radial-1000uf-25v]
  Q2 = LTR-301 [package=ltr-301]  # not connected

nets:
  GND: J1.pin1, Part1.D1/TX, Part1.GND, X2.GND, X3.GND, BATT1.NEG, C1.-
  N1: J1.pin2, Part1.D12/MISO
  N2: Part1.D2, X3.IN1
  N3: Part1.D3, X3.IN2
  N4: Part1.D4, X3.IN3
  N5: Part1.D5, X3.IN4
  N6: Part1.D6, X2.IN1
  N7: Part1.D7, X2.IN2
  N8: Part1.D8, X2.IN3
  N9: Part1.D9, X2.IN4
  N10: Part1.5V, D1.A, C1.+
  N11: MOTOR2.BLUE, X2.BLUE
  N12: MOTOR2.PINK, X2.PINK
  N13: MOTOR2.RED, X2.RED
  N14: MOTOR2.ORANGE, X2.ORANGE
  N15: MOTOR2.YELLOW, X2.YELLOW
  N16: X2.+V, X3.+V, BATT1.POS
  N17: MOTOR3.BLUE, X3.BLUE
  N18: MOTOR3.PINK, X3.PINK
  N19: MOTOR3.RED, X3.RED
  N20: MOTOR3.ORANGE, X3.ORANGE
  N21: MOTOR3.YELLOW, X3.YELLOW

custom parts:
  28BYJ-48 Stepper Motor: 28BYJ-48 gear-reduction stepper motor (small)
  X113647 Stepper Driver Board: A common stepper motor driver board based on ULN2003APG darlington array
  3xAAA Switchable Battery Pack w/Bare Wire: 3xAAA Switchable Battery Pack w/Bare Wire Connectors
