# Fritzing sketch shonkbot_no_motors (saved by Fritzing 0.8.3b)
breadboards: 1

parts:
  Part1 = Arduino Nano (Rev3.0)
  J1 = Piezo Speaker
  R1 = Resistor [tolerance=±5% resistance=10k package=THT]
  D1 = Diode [package=diode-1n4148]
  Receiver_-_blue_tape = LED - 5mm [color="Infrared (850nm)" package="5 mm [THT]"]
  LED_-_black_tape = LED - 5mm [color="Infrared (850nm)" package="5 mm [THT]"]
  VCC1 = 4 x AAA Battery Mount
  C1 = Electrolytic Capacitor [capacitance=1μF package="0405 [SMD, electrolytic]"]

nets:
  N1: Part1.D1/TX, Part1.GND, J1.pin1, Receiver_-_blue_tape.cathode, LED_-_black_tape.cathode, VCC1.-, C1.-
  N2: Part1.D12/MISO, J1.pin2
  N3: Part1.5V, R1.Pin_0, D1.A
  N4: Part1.A0, R1.Pin_1, Receiver_-_blue_tape.anode
  N5: Part1.D13/SCK, LED_-_black_tape.anode
  N6: D1.C, VCC1.+
